# Fritzing sketch schematic (saved by Fritzing 0.9.3b)
breadboards: 1

parts:
  Raspberry_Pi_1 = Raspberry Pi 3 [part_number=RPI-3-V1.2]
  M2 = Dagu DGServo 9g (End View) [part_number=RS001B]
  M1 = Dagu DGServo 9g (End View)
  JP1 = USB Micro-B Connector Breakout [package=micro-b-th]

nets:
  N1: Raspberry_Pi_1.GPIO2, M2.pulse
  N2: Raspberry_Pi_1.GPIO3, M1.pulse
  GND: Raspberry_Pi_1.GND, M2.gnd, M1.gnd, JP1.GND
  VCC: Raspberry_Pi_1.5V, M2.vcc, M1.vcc, JP1.VCC

custom parts:
  USB Micro-B Connector Breakout: USB Micro-B Connector Breakout https://www.robotshop.com/ca/en/usb-micro-b-connector-breakout-board.html
